# Fritzing sketch Smart fan (saved by Fritzing 0.9.3b)
circuit board: 8.46667cm x 5.64444cm
breadboards: 1

parts:
  Part1 = Arduino Uno (Rev3) - ICSP
  IC1 = L293D [package=THT]
  Part2 = LCD1602-I2C
  BAT1 = Battery Holders [package=lipo-1100mAh]
  T1 = LM35 Temperature Sensor [package="TO92 [THT]"]
  Part3 = HC-05 [part_number=HC-05 package="breakout board"]
  F1 = Fan - Ventilador [package=THT]

nets:
  N1: Part1.A0, T1.Vout
  N2: Part1.A4/SDA, Part2.SDA
  N3: Part1.A5/SCL, Part2.SCL
  N4: Part1.D8, IC1.In_2
  N5: Part1.D9_PWM, IC1.0V
  N6: Part1.D10_PWM/SS, IC1.Enable_1
  GND: Part1.GND, Part3.GND
  N7: Part1.D2, Part3.TXD
  N8: Part1.D3_PWM, Part3.RXD
  5V: Part1.5V, Part3.VCC
  N9: IC1.Out_1_(_Controlled_by_Enable_1_), F1.5V
  N10: IC1.Out_2_(_Controlled_by_Enable_1_), F1.GND
  N11: IC1.+Vmotor, BAT1.+
  N12: Part2.GND, BAT1.-
  N13: Part2.VCC, T1.+Vs

custom parts:
  LCD1602-I2C: A standard character display, usually with 2x16 characters. Comes in many colors with LCM1602 IIC attached.
  HC-05: A commonly available HC-05 Bluetooth breakout board.
  Fan - Ventilador: Ventilador de 2 pines, se encuentra comunmente en computadoras de escritorio
